// Logisim project ev_cpu_final.circ as structural Verilog: 4 circuits, main circuit main
module main (
  input  Cin,
  input  [7:0] B,
  input  enB,
  input  [7:0] A,
  input  enA,
  input  invA,
  input  F0,
  input  F1,
  output [7:0] Res,
  output out_10
);

  // Probe on B
  // Probe on A
  ALU_8_Final alu_8_final_1 (
    .enB(enB), .B(B), .ivnA(invA), .enA(enA), .A(A), .F0(F0), .F1(F1), .cin(Cin), .oput(Res), .co(out_10));
  // Probe on Res

  // Notes on the sheet:
  //   ALU
endmodule

module ALU_1bit (
  input  Cin,
  input  InvA,
  input  A,
  input  EnA,
  input  B,
  input  EnB,
  input  F0,
  input  F1,
  output O,
  output Co
);

  wire and_1_out, and_2_out, and_3_out, and_4_out, and_5_out, and_6_out, and_7_out, and_8_out, and_9_out,
       and_10_out, and_11_out, and_12_out, and_13_out, not_1_out, not_2_out, not_3_out, not_4_out, not_5_out,
       or_1_out, xor_1_out, xor_2_out, xor_3_out;

  and and_1 (and_1_out, A, EnA);
  and and_2 (and_2_out, B, EnB);
  not not_1 (not_1_out, F0);
  not not_2 (not_2_out, F1);
  not not_3 (not_3_out, F0);
  not not_4 (not_4_out, F1);
  xor xor_1 (xor_1_out, InvA, and_1_out);
  and and_3 (and_3_out, not_1_out, not_2_out);
  and and_4 (and_4_out, not_3_out, F1);
  and and_5 (and_5_out, F0, not_4_out);
  and and_6 (and_6_out, F0, F1);
  and and_7 (and_7_out, xor_1_out, and_2_out);
  or or_1 (or_1_out, xor_1_out, and_2_out);
  not not_5 (not_5_out, and_2_out);
  and and_8 (and_8_out, and_7_out, and_3_out);
  and and_9 (and_9_out, or_1_out, and_4_out);
  and and_10 (and_10_out, not_5_out, and_5_out);
  and and_11 (and_11_out, and_6_out, xor_1_out, and_2_out);
  xor xor_2 (xor_2_out, and_2_out, xor_1_out);
  and and_12 (and_12_out, and_6_out, xor_2_out, Cin);
  or or_2 (Co, and_11_out, and_12_out);
  xor xor_3 (xor_3_out, Cin, xor_2_out);
  and and_13 (and_13_out, xor_3_out, and_6_out);
  or or_3 (O, and_8_out, and_9_out, and_10_out, and_13_out);
endmodule

module ALU_8bit (
  input  in_1,
  input  in_2,
  input  in_3,
  input  in_4,
  input  in_5,
  input  in_6,
  input  in_7,
  input  in_8,
  input  in_9,
  input  in_10,
  input  in_11,
  input  in_12,
  input  in_13,
  input  in_14,
  input  in_15,
  input  in_16,
  input  in_17,
  input  in_18,
  input  in_19,
  input  in_20,
  input  in_21,
  output out_22,
  output out_23,
  output out_24,
  output out_25,
  output out_26,
  output out_27,
  output out_28,
  output out_29,
  output out_30
);

  wire alu_1bit_1_co, alu_1bit_2_co, alu_1bit_3_co, alu_1bit_4_co, alu_1bit_5_co, alu_1bit_6_co,
       alu_1bit_7_co, cin;

  ALU_1bit alu_1bit_1 (
    .Cin(cin), .InvA(in_10), .A(in_19), .EnA(in_11), .B(in_9), .EnB(in_1), .F0(in_20), .F1(in_21),
    .O(out_29), .Co(alu_1bit_1_co));
  ALU_1bit alu_1bit_2 (
    .Cin(alu_1bit_1_co), .InvA(in_10), .A(in_18), .EnA(in_11), .B(in_8), .EnB(in_1), .F0(in_20), .F1(in_21),
    .O(out_28), .Co(alu_1bit_2_co));
  ALU_1bit alu_1bit_3 (
    .Cin(alu_1bit_2_co), .InvA(in_10), .A(in_17), .EnA(in_11), .B(in_7), .EnB(in_1), .F0(in_20), .F1(in_21),
    .O(out_27), .Co(alu_1bit_3_co));
  ALU_1bit alu_1bit_4 (
    .Cin(alu_1bit_3_co), .InvA(in_10), .A(in_16), .EnA(in_11), .B(in_6), .EnB(in_1), .F0(in_20), .F1(in_21),
    .O(out_26), .Co(alu_1bit_4_co));
  ALU_1bit alu_1bit_5 (
    .Cin(alu_1bit_4_co), .InvA(in_10), .A(in_15), .EnA(in_11), .B(in_5), .EnB(in_1), .F0(in_20), .F1(in_21),
    .O(out_25), .Co(alu_1bit_5_co));
  ALU_1bit alu_1bit_6 (
    .Cin(alu_1bit_5_co), .InvA(in_10), .A(in_14), .EnA(in_11), .B(in_4), .EnB(in_1), .F0(in_20), .F1(in_21),
    .O(out_24), .Co(alu_1bit_6_co));
  ALU_1bit alu_1bit_7 (
    .Cin(alu_1bit_6_co), .InvA(in_10), .A(in_13), .EnA(in_11), .B(in_3), .EnB(in_1), .F0(in_20), .F1(in_21),
    .O(out_23), .Co(alu_1bit_7_co));
  ALU_1bit alu_1bit_8 (
    .Cin(alu_1bit_7_co), .InvA(in_10), .A(in_12), .EnA(in_11), .B(in_2), .EnB(in_1), .F0(in_20), .F1(in_21),
    .O(out_22), .Co(out_30));

  // Other names for the same wires on the sheet: A0 = in_19; A1 = in_18; A2 = in_17; A3 = in_16; A4 = in_15;
  //   A5 = in_14; A6 = in_13; A7 = in_12; B0 = in_9; B1 = in_8; B2 = in_7; B3 = in_6; B4 = in_5; B5 = in_4; B6 = in_3;
  //   B7 = in_2; co = out_30; enA = in_11; enB = in_1; F0 = in_20; F1 = in_21; invA = in_10; out0 = out_29;
  //   out1 = out_28; out2 = out_27; out3 = out_26; out4 = out_25; out5 = out_24; out6 = out_23; out7 = out_22
endmodule

module ALU_8_Final (
  input  [7:0] B,
  input  [7:0] A,
  input  ivnA,
  input  enA,
  input  enB,
  input  F0,
  input  F1,
  input  cin,
  output [7:0] oput,
  output co
);

  wire alu_1bit_1_co, alu_1bit_2_co, alu_1bit_3_co, alu_1bit_4_co, alu_1bit_5_co, alu_1bit_6_co,
       alu_1bit_7_co;

  // Probe on B
  ALU_1bit alu_1bit_1 (
    .Cin(cin), .InvA(ivnA), .A(A[0]), .EnA(enA), .B(B[0]), .EnB(enB), .F0(F0), .F1(F1), .O(oput[0]),
    .Co(alu_1bit_1_co));
  // Probe on oput
  // Probe on A
  ALU_1bit alu_1bit_2 (
    .Cin(alu_1bit_1_co), .InvA(ivnA), .A(A[1]), .EnA(enA), .B(B[1]), .EnB(enB), .F0(F0), .F1(F1),
    .O(oput[1]), .Co(alu_1bit_2_co));
  ALU_1bit alu_1bit_3 (
    .Cin(alu_1bit_2_co), .InvA(ivnA), .A(A[2]), .EnA(enA), .B(B[2]), .EnB(enB), .F0(F0), .F1(F1),
    .O(oput[2]), .Co(alu_1bit_3_co));
  ALU_1bit alu_1bit_4 (
    .Cin(alu_1bit_3_co), .InvA(ivnA), .A(A[3]), .EnA(enA), .B(B[3]), .EnB(enB), .F0(F0), .F1(F1),
    .O(oput[3]), .Co(alu_1bit_4_co));
  ALU_1bit alu_1bit_5 (
    .Cin(alu_1bit_4_co), .InvA(ivnA), .A(A[4]), .EnA(enA), .B(B[4]), .EnB(enB), .F0(F0), .F1(F1),
    .O(oput[4]), .Co(alu_1bit_5_co));
  ALU_1bit alu_1bit_6 (
    .Cin(alu_1bit_5_co), .InvA(ivnA), .A(A[5]), .EnA(enA), .B(B[5]), .EnB(enB), .F0(F0), .F1(F1),
    .O(oput[5]), .Co(alu_1bit_6_co));
  ALU_1bit alu_1bit_7 (
    .Cin(alu_1bit_6_co), .InvA(ivnA), .A(A[6]), .EnA(enA), .B(B[6]), .EnB(enB), .F0(F0), .F1(F1),
    .O(oput[6]), .Co(alu_1bit_7_co));
  ALU_1bit alu_1bit_8 (
    .Cin(alu_1bit_7_co), .InvA(ivnA), .A(A[7]), .EnA(enA), .B(B[7]), .EnB(enB), .F0(F0), .F1(F1),
    .O(oput[7]), .Co(co));

  // Other names for the same wires on the sheet: invA = ivnA; out0 = oput[0]; out1 = oput[1]; out2 = oput[2];
  //   out3 = oput[3]; out4 = oput[4]; out5 = oput[5]; out6 = oput[6]; out7 = oput[7]
endmodule
